# Fritzing sketch PIRMega12V (saved by Fritzing 0.9.2b)

parts:
  ArduinoMegaExt = Arduino Mega 2560 (Rev3)
  R1 = Resistor [resistance=10k tolerance=±5% package=THT]
  BarrelJack12v = Power plug
  PIR = PIR sensor

nets:
  N1: ArduinoMegaExt.D16_PWM/TX2, R1.Pin_0, PIR.SIG
  5V: ArduinoMegaExt.5V, R1.Pin_1, PIR.VCC
  GND: ArduinoMegaExt.GND, BarrelJack12v.GND, PIR.GND
  VIN: ArduinoMegaExt.VIN, BarrelJack12v.VCC
